// Logisim project COA2_Chapter4.circ as structural Verilog: 1 circuit, main circuit main
module main (
  input  B,
  input  C,
  input  A,
  input  D,
  input  A_2,
  input  B_2,
  input  C_2,
  input  D_2,
  input  E,
  input  A_3,
  input  B_3,
  input  C_3,
  input  A_4,
  input  B_4,
  input  C_4,
  input  D_3,
  input  A_5,
  input  B_5,
  input  C_5,
  output X,
  output out_21,
  output out_22,
  output f,
  output out_24
);

  wire and_1_out, and_2_out, and_3_out, and_4_out, and_5_out, and_6_out, and_7_out, and_8_out, and_10_out,
       nor_1_out, nor_2_out, not_1_out, not_2_out, not_3_out, not_4_out, not_5_out, not_6_out, not_7_out,
       not_8_out;

  not not_1 (not_1_out, A);
  and and_1 (and_1_out, not_1_out, D);
  nor nor_1 (nor_1_out, B, C);
  not not_2 (not_2_out, A_3);
  not not_3 (not_3_out, B_3);
  not not_4 (not_4_out, C_3);
  not not_5 (not_5_out, A_4);
  not not_6 (not_6_out, B_4);
  not not_7 (not_7_out, A_5);
  not not_8 (not_8_out, B_2);
  and and_2 (and_2_out, B_5, C_5);
  and and_3 (and_3_out, C_2, D_2, E);
  and and_4 (and_4_out, not_8_out, C_2, D_2);
  and and_5 (and_5_out, not_2_out, not_3_out);
  and and_6 (and_6_out, not_2_out, not_4_out);
  and and_7 (and_7_out, D_3, not_5_out, C_4);
  and and_8 (and_8_out, not_6_out, C_4, D_3);
  nor nor_2 (nor_2_out, A_2, B_2, and_3_out);
  and and_9 (X, nor_1_out, and_1_out);
  or or_1 (out_22, and_5_out, and_6_out);
  and and_10 (and_10_out, B_4, A_4);
  or or_2 (out_24, not_7_out, and_2_out);
  or or_3 (f, and_10_out, and_7_out, and_8_out);
  or or_4 (out_21, nor_2_out, and_4_out);
endmodule
