// Logisim project COA2_Chapter05_BoSoSanh1bit.circ as structural Verilog: 1 circuit, main circuit main
module main (
  input  A,
  input  B,
  output LT,
  output EQ,
  output GT
);

  wire not_1_out, not_2_out;

  not not_1 (not_1_out, A);
  not not_2 (not_2_out, B);
  and and_1 (LT, not_1_out, B);
  xnor xnor_1 (EQ, A, B);
  and and_2 (GT, A, not_2_out);
endmodule
