// Logisim project COA2_Chapter05_BoTru1bit.circ as structural Verilog: 1 circuit, main circuit main
module main (
  input  A,
  input  B,
  output Hieu,
  output Muon
);

  wire not_1_out;

  not not_1 (not_1_out, A);
  xor xor_1 (Hieu, A, B);
  and and_1 (Muon, not_1_out, B);
endmodule
