// Logisim project COA2_Chapter05_MUX81.circ as structural Verilog: 1 circuit, main circuit main
module main (
  input  S2,
  input  S1,
  input  S0,
  input  I0,
  input  I1,
  input  I2,
  input  I3,
  input  I4,
  input  I5,
  input  I6,
  input  I7,
  output Y
);

  wire and_1_out, and_2_out, and_3_out, and_4_out, and_5_out, and_6_out, and_7_out, and_8_out, not_1_out,
       not_2_out, not_3_out;

  not not_1 (not_1_out, S2);
  not not_2 (not_2_out, S1);
  not not_3 (not_3_out, S0);
  and and_1 (and_1_out, not_1_out, not_2_out, not_3_out, I0);
  and and_2 (and_2_out, not_1_out, not_2_out, S0, I1);
  and and_3 (and_3_out, not_1_out, S1, not_3_out, I2);
  and and_4 (and_4_out, not_1_out, I3);
  buf and_5 (and_5_out, not_1_out);  // AND_Gate
  buf and_6 (and_6_out, not_1_out);  // AND_Gate
  // AND_Gate and_7 has open pins: out=and_7_out
  // AND_Gate and_8 has open pins: out=and_8_out
  // OR_Gate or_1 has open pins: out=Y
endmodule
