// Logisim project COA_Chapter05_BoCong2Bits.circ as structural Verilog: 1 circuit, main circuit main
module main (
  input  A_0,
  input  A_1,
  input  B_0,
  input  B_1,
  output R_0,
  output R_1,
  output C
);

  wire and_1_out, and_2_out, and_3_out, xor_2_out;

  xor xor_1 (R_0, A_0, B_0);
  xor xor_2 (xor_2_out, A_1, B_1);
  and and_1 (and_1_out, A_0, B_0);
  xor xor_3 (R_1, and_1_out, xor_2_out);
  and and_2 (and_2_out, B_1, A_1);
  and and_3 (and_3_out, and_1_out, xor_2_out);
  or or_1 (C, and_3_out, and_2_out);
endmodule
