// Logisim project COA_Chapter05_BoCongToanPhan.circ as structural Verilog: 4 circuits, main circuit main
module FA_4bits (
  input  A,
  input  B,
  input  Cin,
  output S,
  output Cout
);

  wire and_1_out, and_2_out, xor_2_out;

  ExactlyOne xor_1 (.out(S), .in0(A), .in1(B), .in2(Cin));
  xor xor_2 (xor_2_out, A, B);
  and and_1 (and_1_out, A, B);
  and and_2 (and_2_out, Cin, xor_2_out);
  or or_1 (Cout, and_1_out, and_2_out);
endmodule

module main (
  input  A0,
  input  Cin_Zero,
  input  A1,
  input  A2,
  input  B3,
  input  A3,
  input  B2,
  input  B1,
  input  B0,
  output Equal_to_Zero
);

  wire bu2_4bits_1_t, bu2_4bits_1_x, bu2_4bits_1_y, bu2_4bits_1_z, fa_4bits_1_cout, fa_4bits_1_s,
       fa_4bits_2_cout, fa_4bits_2_s, fa_4bits_3_cout, fa_4bits_3_s, fa_4bits_4_s;

  FA_4bits fa_4bits_1 (.A(A0), .B(bu2_4bits_1_x), .Cin(Cin_Zero), .S(fa_4bits_1_s), .Cout(fa_4bits_1_cout));
  Bu2_4bits bu2_4bits_1 (
    .B3(B3), .B2(B2), .B1(B1), .B0(B0), .X(bu2_4bits_1_x), .Y(bu2_4bits_1_y), .Z(bu2_4bits_1_z),
    .T(bu2_4bits_1_t));
  FA_4bits fa_4bits_2 (.A(A1), .B(bu2_4bits_1_y), .Cin(fa_4bits_1_cout), .S(fa_4bits_2_s), .Cout(fa_4bits_2_cout));
  FA_4bits fa_4bits_3 (.A(A2), .B(bu2_4bits_1_z), .Cin(fa_4bits_2_cout), .S(fa_4bits_3_s), .Cout(fa_4bits_3_cout));
  FA_4bits fa_4bits_4 (.A(A3), .B(bu2_4bits_1_t), .Cin(fa_4bits_3_cout), .S(fa_4bits_4_s));  // open: Cout
  nor nor_1 (Equal_to_Zero, fa_4bits_1_s, fa_4bits_4_s, fa_4bits_3_s, fa_4bits_2_s);
  Multiplexer multiplexer_1 (.sel(Equal_to_Zero));  // open: in0, in1, out
endmodule

module Bu2_4bits (
  input  B3,
  input  B2,
  input  B1,
  input  B0,
  output X,
  output Y,
  output Z,
  output T
);

  wire or_1_out, or_2_out;

  or or_1 (or_1_out, B0, B1);
  xor xor_1 (Z, B1, B0);
  xor xor_2 (Y, B2, or_1_out);
  or or_2 (or_2_out, B2, or_1_out);
  xor xor_3 (X, B3, or_2_out);

  assign T = B0;
endmodule

module MachSoSanh (
  input  A,
  input  B,
  output LT,
  output EQ,
  output GT
);

  wire not_1_out, not_2_out;

  not not_1 (not_1_out, A);
  not not_2 (not_2_out, B);
  and and_1 (LT, not_1_out, B);
  and and_2 (GT, A, not_2_out);
  xnor xnor_1 (EQ, A, B);
endmodule
