// Logisim project COA_Chapter05_BoTruToanPhan.circ as structural Verilog: 2 circuits, main circuit FS_1bit
module FS_1bit (
  input  A,
  input  B,
  input  Bin,
  output Hieu,
  output Muon
);

  wire and_1_out, and_2_out, not_1_out, or_1_out, xor_1_out;

  not not_1 (not_1_out, A);
  xor xor_1 (xor_1_out, A, B);
  or or_1 (or_1_out, not_1_out, B);
  and and_1 (and_1_out, not_1_out, B);
  and and_2 (and_2_out, Bin, or_1_out);
  or or_2 (Muon, and_2_out, and_1_out);
  xor xor_2 (Hieu, xor_1_out, Bin);
endmodule

module FS (
  input  A0,
  input  A1,
  input  A2,
  input  B0,
  input  B1,
  input  B2,
  input  in_7,
  input  A3,
  input  B3,
  output [3:0] C,
  output Bit_Du_Ra
);

  wire fs_1bit_1_muon, fs_1bit_3_muon, fs_1bit_4_muon;

  FS_1bit fs_1bit_1 (.A(A0), .B(B0), .Bin(in_7), .Muon(fs_1bit_1_muon));  // open: Hieu
  FS_1bit fs_1bit_2 (.A(A3), .B(B3), .Bin(fs_1bit_4_muon), .Muon(Bit_Du_Ra));  // open: Hieu
  Multiplexer #(.width(4)) multiplexer_1 (.in0({A3, A2, A1, A0}), .in1({B3, B2, B1, B0}), .out(C), .sel(Bit_Du_Ra));
  FS_1bit fs_1bit_3 (.A(A1), .B(B1), .Bin(fs_1bit_1_muon), .Muon(fs_1bit_3_muon));  // open: Hieu
  FS_1bit fs_1bit_4 (.A(A2), .B(B2), .Bin(fs_1bit_3_muon), .Muon(fs_1bit_4_muon));  // open: Hieu
endmodule
