// Logisim project COA_Chapter05_Bu2.circ as structural Verilog: 2 circuits, main circuit main
module main (
  input  A,
  input  B,
  input  C,
  input  lsb_1,
  output X,
  output Y,
  output Z
);

  wire and_1_out, not_1_out, not_2_out, not_3_out;

  not not_1 (not_1_out, A);
  not not_2 (not_2_out, B);
  not not_3 (not_3_out, C);
  and and_1 (and_1_out, not_3_out, not_2_out);
  xor xor_1 (Z, not_3_out, lsb_1);
  xor xor_2 (X, and_1_out, not_1_out);
  xor xor_3 (Y, not_2_out, not_3_out);

  // Notes on the sheet:
  //   3bits
endmodule

module main1 (
  input  A,
  input  B,
  input  C,
  input  D,
  output X,
  output Y,
  output Z,
  output T
);

  wire or_1_out, or_2_out;

  or or_1 (or_1_out, D, C);
  xor xor_1 (Z, C, D);
  xor xor_2 (Y, B, or_1_out);
  or or_2 (or_2_out, B, or_1_out);
  xor xor_3 (X, A, or_2_out);

  assign T = D;

  // Notes on the sheet:
  //   4bits
endmodule
