// Logisim project COA_Chapter05_Decoder3to8.circ as structural Verilog: 1 circuit, main circuit main
module main (
  input  A,
  input  B,
  input  Cin,
  output Y0,
  output Cout,
  output Y1,
  output Y2,
  output Y3,
  output Y4,
  output Y5,
  output Y6,
  output Sum,
  output Y7
);

  wire not_1_out, not_2_out, not_3_out;

  not not_1 (not_1_out, A);
  not not_2 (not_2_out, B);
  not not_3 (not_3_out, Cin);
  and and_1 (Y0, not_1_out, not_2_out, not_3_out);
  and and_2 (Y1, not_1_out, not_2_out, Cin);
  and and_3 (Y2, not_1_out, B, not_3_out);
  and and_4 (Y3, not_1_out, B, Cin);
  and and_5 (Y4, A, not_2_out, not_3_out);
  and and_6 (Y5, A, not_2_out, Cin);
  and and_7 (Y6, A, B, not_3_out);
  and and_8 (Y7, A, B, Cin);
  or or_1 (Sum, Y1, Y2, Y4, Y7);
  or or_2 (Cout, Y3, Y5, Y6, Y7);
endmodule
