// Logisim project COA2_Lab01_Circuit1.circ as structural Verilog: 1 circuit, main circuit main
module main (
  input  A,
  input  B,
  input  C,
  output out_4,
  output out_5,
  output out_6,
  output out_7,
  output out_8,
  output out_9,
  output out_10,
  output out_11,
  output out_12,
  output out_13
);

  wire nand_2_out;

  ExactlyOne xor_1 (.out(out_11), .in0(B), .in1(A), .in2(C));
  nand nand_1 (out_12, C, A, B);
  nand nand_2 (nand_2_out, A, B);
  not not_1 (out_6, A);
  buf or_1 (out_8, A);  // OR_Gate
  and and_1 (out_9, A, B);
  xnor xnor_1 (out_10, A, B);
  xor xor_2 (out_4, A, B);
  nor nor_1 (out_5, A, B);
  nand nand_3 (out_7, A, B);
  nand nand_4 (out_13, nand_2_out, C);

  // Notes on the sheet:
  //   TN1
endmodule
