// Logisim project COA2_Lab01_Circuit2.circ as structural Verilog: 1 circuit, main circuit main
module main (
  input  X,
  input  Y,
  input  Z,
  output EQ5,
  output EQ4,
  output EQ1,
  output EQ2,
  output EQ3
);

  wire and_1_out, and_2_out, and_3_out, and_4_out, nand_1_out, nor_1_out, not_1_out, not_2_out, not_3_out,
       or_1_out, or_2_out, or_3_out, or_4_out;

  not not_1 (not_1_out, X);
  not not_2 (not_2_out, X);
  not not_3 (not_3_out, Y);
  and and_1 (and_1_out, not_1_out, Y);
  and and_2 (and_2_out, not_2_out, not_3_out);
  nand nand_1 (nand_1_out, X, Y);
  and and_3 (and_3_out, Y, Z);
  or or_1 (or_1_out, X, and_1_out);
  or or_2 (or_2_out, X, Y);
  xnor xnor_1 (EQ4, X, or_1_out);
  nor nor_1 (nor_1_out, X, Y);
  or or_3 (or_3_out, X, and_3_out);
  xnor xnor_2 (EQ5, or_2_out, or_1_out);
  xnor xnor_3 (EQ1, nor_1_out, and_2_out);
  xnor xnor_4 (EQ2, and_2_out, nand_1_out);
  or or_4 (or_4_out, X, Z);
  and and_4 (and_4_out, or_2_out, or_4_out);
  xnor xnor_5 (EQ3, or_3_out, and_4_out);

  // Notes on the sheet:
  //   TN2
endmodule
