// Logisim project COA2_Lab02_3.2.circ as structural Verilog: 1 circuit, main circuit main
module main (
  input  [7:0] Data_in,
  input  [1:0] write_addr,
  input  Enable,
  input  [1:0] read_addr,
  output [7:0] out_5
);

  wire clock_1_out, decoder_1_out0, decoder_1_out1, decoder_1_out2, decoder_1_out3;
  wire [7:0] register_1_q, register_2_q, register_3_q, register_4_q;

  Clock clock_1 (.out(clock_1_out));
  Decoder #(.select(2)) decoder_1 (
    .out0(decoder_1_out0), .out1(decoder_1_out1), .out2(decoder_1_out2), .out3(decoder_1_out3),
    .sel(write_addr), .en(Enable));
  Register register_1 (.D(Data_in), .en(decoder_1_out0), .clk(clock_1_out), .Q(register_1_q));  // open: clr
  Register register_2 (.D(Data_in), .en(decoder_1_out1), .clk(clock_1_out), .Q(register_2_q));  // open: clr
  Register register_3 (.D(Data_in), .en(decoder_1_out2), .clk(clock_1_out), .Q(register_3_q));  // open: clr
  Register register_4 (.D(Data_in), .en(decoder_1_out3), .clk(clock_1_out), .Q(register_4_q));  // open: clr
  Multiplexer #(.select(2), .width(8)) multiplexer_1 (
    .in0(register_1_q), .in1(register_2_q), .in2(register_3_q), .in3(register_4_q), .out(out_5),
    .sel(read_addr));
endmodule
